// Logisim project 기말프로젝트.circ as structural Verilog: 12 circuits, main circuit main
module main (
  input  _7,
  input  _6,
  input  _5,
  input  _4,
  input  _3,
  input  _2,
  input  _1
);

  wire encode_1_a, encode_1_b, encode_1_c, ic_74hc42_1_y1, ic_74hc42_1_y2, ic_74hc42_1_y3, ic_74hc42_1_y4,
       ic_74hc42_1_y5, ic_74hc42_1_y6, ic_74hc42_1_y7, \n7_segment_디코더_1_a_2 , \n7_segment_디코더_1_b_2 ,
       \n7_segment_디코더_1_c_2 , \n7_segment_디코더_1_d , \n7_segment_디코더_1_e , \n7_segment_디코더_1_f ,
       \n7_segment_디코더_1_g ;

  encode encode_1 (
    ._7(_7), ._6(_6), ._5(_5), ._4(_4), ._3(_3), ._2(_2), ._1(_1), .b(encode_1_b), .c(encode_1_c),
    .a(encode_1_a));  // open: _0
  ic_74hc42 ic_74hc42_1 (
    .A(encode_1_a), .B(encode_1_b), .C(encode_1_c), .y1(ic_74hc42_1_y1), .y2(ic_74hc42_1_y2),
    .y3(ic_74hc42_1_y3), .y4(ic_74hc42_1_y4), .y5(ic_74hc42_1_y5), .y6(ic_74hc42_1_y6), .y7(ic_74hc42_1_y7));
  \_7_segment_디코더  \u_7_segment_디코더_1  (
    .A(encode_1_a), .B(encode_1_b), .C(encode_1_c), .a_2(\n7_segment_디코더_1_a_2 ),
    .b_2(\n7_segment_디코더_1_b_2 ), .c_2(\n7_segment_디코더_1_c_2 ), .d(\n7_segment_디코더_1_d ),
    .e(\n7_segment_디코더_1_e ), .f(\n7_segment_디코더_1_f ), .g(\n7_segment_디코더_1_g ));
  LED u__1 (.in(ic_74hc42_1_y1));
  LED u__2 (.in(ic_74hc42_1_y2));
  LED u__3 (.in(ic_74hc42_1_y3));
  LED u__4 (.in(ic_74hc42_1_y4));
  LED u__5 (.in(ic_74hc42_1_y5));
  LED u__6 (.in(ic_74hc42_1_y6));
  LED u__7 (.in(ic_74hc42_1_y7));
  _7_Segment_Display u_7_segment_display_1 (
    .g(\n7_segment_디코더_1_g ), .f(\n7_segment_디코더_1_f ), .a(\n7_segment_디코더_1_a_2 ),
    .b(\n7_segment_디코더_1_b_2 ), .e(\n7_segment_디코더_1_e ), .d(\n7_segment_디코더_1_d ), .c(\n7_segment_디코더_1_c_2 ));  // open: dp
endmodule

module \_7_segment_디코더  (
  input  A,
  input  B,
  input  C,
  output a_2,
  output b_2,
  output c_2,
  output d,
  output e,
  output f,
  output g
);

  wire and_1_out, and_2_out, and_3_out, and_4_out, and_5_out, and_6_out, and_7_out, and_8_out, and_9_out,
       and_10_out, and_11_out, and_12_out, and_13_out, and_14_out, and_15_out, and_16_out, and_17_out,
       not_1_out, not_2_out, not_3_out, not_4_out, not_5_out, not_6_out, not_7_out, not_8_out, not_9_out,
       not_10_out, not_11_out, not_12_out, not_13_out, not_14_out, not_15_out, not_16_out, not_17_out,
       not_18_out, not_19_out, not_20_out, not_21_out, or_1_out, or_2_out, or_3_out, or_6_out, or_7_out,
       or_10_out, or_11_out;

  not not_1 (not_1_out, A);
  not not_2 (not_2_out, C);
  not not_3 (not_3_out, B);
  not not_4 (not_4_out, C);
  not not_5 (not_5_out, B);
  not not_6 (not_6_out, B);
  not not_7 (not_7_out, A);
  not not_8 (not_8_out, C);
  not not_9 (not_9_out, C);
  not not_10 (not_10_out, B);
  not not_11 (not_11_out, C);
  not not_12 (not_12_out, B);
  not not_13 (not_13_out, A);
  not not_14 (not_14_out, B);
  and and_1 (and_1_out, not_1_out, not_2_out);
  not not_15 (not_15_out, A);
  and and_2 (and_2_out, not_3_out, not_4_out);
  or or_1 (or_1_out, not_5_out, C);
  not not_16 (not_16_out, A);
  not not_17 (not_17_out, C);
  not not_18 (not_18_out, A);
  not not_19 (not_19_out, C);
  and and_3 (and_3_out, A, not_6_out);
  and and_4 (and_4_out, not_7_out, not_8_out);
  and and_5 (and_5_out, B, not_9_out);
  and and_6 (and_6_out, not_10_out, not_11_out);
  and and_7 (and_7_out, A, not_12_out);
  not not_20 (not_20_out, C);
  and and_8 (and_8_out, not_13_out, B);
  and and_9 (and_9_out, A, not_14_out);
  not not_21 (not_21_out, C);
  or or_2 (or_2_out, and_1_out, B);
  and and_10 (and_10_out, A, C);
  or or_3 (or_3_out, not_15_out, and_2_out);
  and and_11 (and_11_out, B, C);
  or or_4 (c_2, or_1_out, A);
  and and_12 (and_12_out, not_16_out, not_17_out);
  and and_13 (and_13_out, not_18_out, B);
  and and_14 (and_14_out, B, not_19_out);
  and and_15 (and_15_out, and_3_out, C);
  or or_5 (e, and_4_out, and_5_out);
  or or_6 (or_6_out, and_6_out, and_7_out);
  and and_16 (and_16_out, A, not_20_out);
  or or_7 (or_7_out, and_8_out, and_9_out);
  and and_17 (and_17_out, A, not_21_out);
  or or_8 (a_2, or_2_out, and_10_out);
  or or_9 (b_2, or_3_out, and_11_out);
  or or_10 (or_10_out, and_12_out, and_13_out);
  or or_11 (or_11_out, and_14_out, and_15_out);
  or or_12 (f, or_6_out, and_16_out);
  or or_13 (g, or_7_out, and_17_out);
  or or_14 (d, or_10_out, or_11_out);
endmodule

module encode (
  input  _7,
  input  _6,
  input  _5,
  input  _4,
  input  _3,
  input  _2,
  input  _1,
  input  _0,
  output b,
  output c,
  output a
);

  or or_1 (c, _1, _3, _5, _7);
  or or_2 (b, _2, _3, _6, _7);
  or or_3 (a, _4, _5, _6, _7);
endmodule

module ic_74hc42 (
  input  A,
  input  B,
  input  C,
  output y1,
  output y2,
  output y3,
  output y4,
  output y5,
  output y6,
  output y7
);

  wire not_1_out, not_2_out, not_3_out, not_4_out, not_5_out, not_6_out, not_7_out, not_8_out, not_9_out;

  not not_1 (not_1_out, A);
  not not_2 (not_2_out, B);
  not not_3 (not_3_out, A);
  not not_4 (not_4_out, C);
  not not_5 (not_5_out, A);
  not not_6 (not_6_out, B);
  not not_7 (not_7_out, C);
  not not_8 (not_8_out, B);
  not not_9 (not_9_out, C);
  and and_1 (y7, A, B, C);
  and and_2 (y1, not_1_out, not_2_out, C);
  and and_3 (y2, not_3_out, B, not_4_out);
  and and_4 (y3, not_5_out, B, C);
  and and_5 (y4, A, not_6_out, not_7_out);
  and and_6 (y5, A, not_8_out, C);
  and and_7 (y6, A, B, not_9_out);
endmodule

module \내부_버튼_제어기  (
  input  _7,
  input  _6,
  input  _5,
  input  _4,
  input  _3,
  input  _2,
  input  _1,
  input  in_8,
  output c,
  output b,
  output a,
  output out_12,
  output out_13,
  output out_14
);

  wire and_1_out, and_2_out, and_3_out, and_4_out, and_5_out, clock_1_out, not_1_out, or_2_out, or_6_out,
       or_7_out, t_ff_1_qn, t_ff_2_qn, xor_1_out, xor_2_out, xor_3_out;

  // OR_Gate or_1 is placed but not wired
  or or_2 (or_2_out, xor_1_out, xor_2_out, xor_3_out);
  Clock clock_1 (.out(clock_1_out));
  not not_1 (not_1_out, in_8);
  and and_1 (and_1_out, clock_1_out, or_2_out);
  or or_3 (c, _1, _3, _5, _7);
  or or_4 (b, _2, _3, _6, _7);
  or or_5 (a, _4, _5, _6, _7);
  xor xor_1 (xor_1_out, c, out_12);
  and and_2 (and_2_out, not_1_out, out_12);
  T_Flip_Flop t_ff_1 (.clk(and_1_out), .T(1'b1), .Q(out_12), .Qn(t_ff_1_qn));  // open: preset, reset, en
  and and_3 (and_3_out, t_ff_1_qn, in_8);
  xor xor_2 (xor_2_out, b, out_13);
  or or_6 (or_6_out, and_2_out, and_3_out);
  and and_4 (and_4_out, and_2_out, out_13);
  T_Flip_Flop t_ff_2 (.clk(and_1_out), .T(or_6_out), .Q(out_13), .Qn(t_ff_2_qn));  // open: preset, reset, en
  and and_5 (and_5_out, t_ff_2_qn, and_3_out);
  xor xor_3 (xor_3_out, a, out_14);
  or or_7 (or_7_out, and_4_out, and_5_out);
  T_Flip_Flop t_ff_3 (.clk(and_1_out), .T(or_7_out), .Q(out_14));  // open: Qn, preset, reset, en
endmodule

module \기말프로젝트  (
  input  in_1,
  input  in_2,
  input  in_3
);

  wire _1_out, _2_out, _3_out, and_1_out, and_2_out, clock_1_out, clock_2_out, \n7_segment_디코더_1_a_2 ,
       \n7_segment_디코더_1_b_2 , \n7_segment_디코더_1_c_2 , \n7_segment_디코더_1_d , \n7_segment_디코더_1_e ,
       \n7_segment_디코더_1_f , \n7_segment_디코더_1_g , \비교기_1_x보다y가크다 , \비교기_1_x와y는같다 , \비교기_1_y보다x가크다 ,
       \인코더_1__1층_led , \인코더_1__2층_led , \인코더_1__3층_led , \인코더_1_b0 , \인코더_1_b1 , \층수_메모리_b0 , \층수_메모리_b1 ;

  Button _3 (.out(_3_out));
  LED led_1 (.in(\인코더_1__3층_led ));
  LED led_2 (.in(\인코더_1__2층_led ));
  Button _2 (.out(_2_out));
  LED led_3 (.in(\인코더_1__1층_led ));
  Button _1 (.out(_1_out));
  \인코더  \u_인코더_1  (
    ._1(_1_out), ._2(_2_out), ._3(_3_out), .claer(and_2_out), .b1(\인코더_1_b1 ), .b0(\인코더_1_b0 ),
    .\_1층_LED (\인코더_1__1층_led ), .\_2층_LED (\인코더_1__2층_led ), .\_3층_LED (\인코더_1__3층_led ));
  Comparator #(.width(3)) comparator_1 ();  // open: a, b, gt, eq, lt
  Clock clock_1 (.out(clock_1_out));
  and and_1 (and_1_out, ~\인코더_1_b0 , ~\인코더_1_b1 );  // AND_Gate
  and and_2 (and_2_out, \비교기_1_x와y는같다 , clock_2_out);
  \현재_층수_메모리  \u_층수_메모리  (
    .CLOCK(clock_1_out), .ENABLE(and_1_out), .B1(\층수_메모리_b1 ), .B0(\층수_메모리_b0 ), .UP(\비교기_1_x보다y가크다 ),
    .DOWN(\비교기_1_y보다x가크다 ));  // open: CLEAR
  \비교기  \u_비교기_1  (
    .X1(\층수_메모리_b1 ), .X0(\층수_메모리_b0 ), .Y1(\인코더_1_b1 ), .Y0(\인코더_1_b0 ), .\x보다y가크다 (\비교기_1_x보다y가크다 ),
    .\y보다x가크다 (\비교기_1_y보다x가크다 ), .\x와y는같다 (\비교기_1_x와y는같다 ));  // open: x와y는같지않다
  Clock clock_2 (.out(clock_2_out));
  \_7_segment_디코더  \u_7_segment_디코더_1  (
    .A(in_1), .B(\층수_메모리_b1 ), .C(\층수_메모리_b0 ), .a_2(\n7_segment_디코더_1_a_2 ), .b_2(\n7_segment_디코더_1_b_2 ),
    .c_2(\n7_segment_디코더_1_c_2 ), .d(\n7_segment_디코더_1_d ), .e(\n7_segment_디코더_1_e ),
    .f(\n7_segment_디코더_1_f ), .g(\n7_segment_디코더_1_g ));
  _7_Segment_Display u_7_segment_display_1 (
    .g(\n7_segment_디코더_1_g ), .f(\n7_segment_디코더_1_f ), .a(\n7_segment_디코더_1_a_2 ),
    .b(\n7_segment_디코더_1_b_2 ), .e(\n7_segment_디코더_1_e ), .d(\n7_segment_디코더_1_d ), .c(\n7_segment_디코더_1_c_2 ));  // open: dp
  // OR_Gate or_1 is placed but not wired
endmodule

module \현재_층수_메모리  (
  input  CLOCK,
  input  ENABLE,
  input  CLEAR,
  input  UP,
  input  DOWN,
  output B1,
  output B0
);

  wire and_1_out, and_2_out, and_3_out, and_4_out, and_5_out, not_1_out, not_2_out, not_3_out, not_4_out,
       not_5_out, not_6_out, not_7_out, not_8_out, not_9_out, not_10_out, not_11_out, or_1_out, or_2_out;

  not not_1 (not_1_out, ENABLE);
  T_Flip_Flop t_ff_1 (.clk(CLOCK), .T(or_1_out), .Q(B1), .reset(CLEAR), .en(not_1_out));  // open: Qn, preset
  or or_1 (or_1_out, and_1_out, and_2_out);
  or or_2 (or_2_out, and_3_out, and_4_out, and_5_out);
  T_Flip_Flop t_ff_2 (.clk(CLOCK), .T(or_2_out), .Q(B0), .reset(CLEAR), .en(not_2_out));  // open: Qn, preset
  not not_2 (not_2_out, ENABLE);
  and and_1 (and_1_out, B0, not_3_out, UP, not_4_out);
  and and_2 (and_2_out, B1, not_5_out, not_6_out, DOWN);
  and and_3 (and_3_out, not_7_out, UP, not_8_out, B0);
  and and_4 (and_4_out, not_9_out, B1, DOWN);
  and and_5 (and_5_out, B1, not_10_out, UP, not_11_out);
  not not_3 (not_3_out, B1);
  not not_4 (not_4_out, DOWN);
  not not_5 (not_5_out, B0);
  not not_6 (not_6_out, UP);
  not not_7 (not_7_out, B1);
  not not_8 (not_8_out, DOWN);
  not not_9 (not_9_out, UP);
  not not_10 (not_10_out, B0);
  not not_11 (not_11_out, DOWN);

  // Notes on the sheet:
  //   a
  //   b
  //   x
  //   y
endmodule

module \인코더  (
  input  claer,
  input  _1,
  input  _2,
  input  _3,
  output \_1층_LED ,
  output \_2층_LED ,
  output \_3층_LED ,
  output b1,
  output b0
);

  wire d_ff_1_qn, d_ff_2_qn, d_ff_3_qn, not_1_out, not_2_out, not_3_out, or_3_out;

  not not_1 (not_1_out, or_3_out);
  not not_2 (not_2_out, or_3_out);
  not not_3 (not_3_out, or_3_out);
  D_Flip_Flop d_ff_1 (
    .clk(_1), .D(d_ff_1_qn), .Q(\_1층_LED ), .Qn(d_ff_1_qn), .en(not_1_out), .reset(claer));  // open: preset
  D_Flip_Flop d_ff_2 (
    .clk(_2), .D(d_ff_2_qn), .Q(\_2층_LED ), .Qn(d_ff_2_qn), .en(not_2_out), .reset(claer));  // open: preset
  D_Flip_Flop d_ff_3 (
    .clk(_3), .D(d_ff_3_qn), .Q(\_3층_LED ), .Qn(d_ff_3_qn), .en(not_3_out), .reset(claer));  // open: preset
  or or_1 (b0, \_1층_LED , \_3층_LED );
  or or_2 (b1, \_2층_LED , \_3층_LED );
  or or_3 (or_3_out, b0, b1);
endmodule

module \비교기  (
  input  X1,
  input  X0,
  input  Y1,
  input  Y0,
  output \x보다y가크다 ,
  output \y보다x가크다 ,
  output \x와y는같지않다 ,
  output \x와y는같다 
);

  wire and_1_out, and_2_out, and_3_out, and_4_out, and_5_out, and_6_out, and_7_out, and_8_out, and_9_out,
       and_10_out, and_11_out, and_12_out, and_13_out, and_14_out, not_1_out, not_2_out, not_3_out,
       not_4_out, not_5_out, not_6_out, not_7_out, not_8_out, not_9_out, not_10_out, not_11_out, not_12_out,
       not_13_out, not_14_out, not_15_out, not_16_out, not_17_out, not_18_out, not_19_out, not_20_out;

  not not_1 (not_1_out, X1);
  not not_2 (not_2_out, X0);
  and and_1 (and_1_out, not_1_out, not_2_out, Y0);
  not not_3 (not_3_out, X1);
  and and_2 (and_2_out, not_3_out, Y1);
  not not_4 (not_4_out, X0);
  and and_3 (and_3_out, not_4_out, Y1, Y0);
  not not_5 (not_5_out, Y1);
  and and_4 (and_4_out, X0, not_5_out, not_6_out);
  not not_6 (not_6_out, Y0);
  and and_5 (and_5_out, X1, not_7_out);
  not not_7 (not_7_out, Y1);
  and and_6 (and_6_out, X1, X0, not_8_out);
  not not_8 (not_8_out, Y0);
  not not_9 (not_9_out, X0);
  and and_7 (and_7_out, not_9_out, Y0);
  not not_10 (not_10_out, X1);
  and and_8 (and_8_out, not_10_out, Y1);
  and and_9 (and_9_out, X0, not_11_out);
  not not_11 (not_11_out, Y0);
  and and_10 (and_10_out, X1, not_12_out);
  not not_12 (not_12_out, Y1);
  not not_13 (not_13_out, X1);
  not not_14 (not_14_out, X0);
  not not_15 (not_15_out, Y1);
  not not_16 (not_16_out, Y0);
  not not_17 (not_17_out, X1);
  not not_18 (not_18_out, Y1);
  not not_19 (not_19_out, X0);
  not not_20 (not_20_out, Y0);
  or or_1 (\x보다y가크다 , and_1_out, and_2_out, and_3_out);
  or or_2 (\y보다x가크다 , and_4_out, and_5_out, and_6_out);
  or or_3 (\x와y는같지않다 , and_7_out, and_8_out, and_9_out, and_10_out);
  and and_11 (and_11_out, not_13_out, not_14_out, not_15_out, not_16_out);
  and and_12 (and_12_out, not_17_out, X0, not_18_out, Y0);
  and and_13 (and_13_out, X1, not_19_out, Y1, not_20_out);
  and and_14 (and_14_out, X1, X0, Y1, Y0);
  or or_4 (\x와y는같다 , and_11_out, and_12_out, and_13_out, and_14_out);
endmodule

module _3bit_Sequential_Logic_Circuits (
  input  CLOCK,
  input  Preset,
  input  ENABLE,
  input  UP,
  input  DOWN,
  output B2,
  output B1,
  output B0
);

  wire and_1_out, and_2_out, and_3_out, and_4_out, and_5_out, and_6_out, and_7_out, and_8_out, and_9_out,
       and_10_out, and_11_out, and_12_out, and_13_out, not_1_out, not_2_out, not_3_out, not_4_out, not_5_out,
       not_6_out, or_1_out, or_2_out, or_3_out;

  not not_1 (not_1_out, ENABLE);
  T_Flip_Flop A (.clk(CLOCK), .T(or_3_out), .Q(B2), .preset(Preset), .en(not_1_out));  // open: Qn, reset
  or or_1 (or_1_out, and_3_out, and_4_out, and_5_out, and_6_out, and_7_out, and_8_out);
  or or_2 (or_2_out, and_9_out, and_10_out, and_11_out, and_12_out, and_13_out);
  T_Flip_Flop B (.clk(CLOCK), .T(or_1_out), .Q(B1), .en(not_2_out));  // open: Qn, preset, reset
  not not_2 (not_2_out, ENABLE);
  or or_3 (or_3_out, and_1_out, and_2_out);
  T_Flip_Flop C (.clk(CLOCK), .T(or_2_out), .Q(B0), .en(not_3_out));  // open: Qn, preset, reset
  not not_3 (not_3_out, ENABLE);
  and and_1 (and_1_out, ~B2, ~DOWN, B1, UP, B0);  // AND_Gate
  and and_2 (and_2_out, B2, ~B1, ~B0, ~UP, DOWN);  // AND_Gate
  and and_3 (and_3_out, ~B2, ~B1, B0, UP, ~DOWN);  // AND_Gate
  and and_4 (and_4_out, ~B2, B1, ~B0, ~UP, DOWN);  // AND_Gate
  and and_5 (and_5_out, ~B2, B1, B0, UP, ~DOWN);  // AND_Gate
  and and_6 (and_6_out, B2, ~B1, ~B0, ~UP, DOWN);  // AND_Gate
  and and_7 (and_7_out, B2, ~B1, B0, UP, ~DOWN);  // AND_Gate
  and and_8 (and_8_out, B2, B1, ~B0, ~UP, DOWN);  // AND_Gate
  and and_9 (and_9_out, B2, ~UP, DOWN);  // AND_Gate
  and and_10 (and_10_out, B1, ~UP, DOWN);  // AND_Gate
  not not_4 (not_4_out, B0);
  and and_11 (and_11_out, B1, not_4_out, UP, ~DOWN);  // AND_Gate
  not not_5 (not_5_out, B2);
  and and_12 (and_12_out, not_5_out, B0, UP, ~DOWN);  // AND_Gate
  and and_13 (and_13_out, B2, ~B1, UP, not_6_out);  // AND_Gate
  not not_6 (not_6_out, DOWN);

  // Notes on the sheet:
  //   C
  //   A
  //   B
  //   X
  //   Y
endmodule

module _7_sD_FF_ENCODER (
  input  claer,
  input  _1,
  input  _2,
  input  _3,
  input  _4,
  input  _5,
  input  _6,
  input  _7,
  output \_1층_LED ,
  output \_2층_LED ,
  output \_3층_LED ,
  output \_4층_LED ,
  output \_5층_LED ,
  output \_6층_LED ,
  output \_7층_LED ,
  output b1,
  output b0,
  output b2
);

  wire d_ff_1_qn, d_ff_2_qn, d_ff_3_qn, d_ff_4_qn, d_ff_5_qn, d_ff_6_qn, d_ff_7_qn, not_1_out, or_4_out;

  D_Flip_Flop d_ff_1 (
    .clk(_1), .D(d_ff_1_qn), .Q(\_1층_LED ), .Qn(d_ff_1_qn), .en(not_1_out), .reset(claer));  // open: preset
  D_Flip_Flop d_ff_2 (
    .clk(_2), .D(d_ff_2_qn), .Q(\_2층_LED ), .Qn(d_ff_2_qn), .en(not_1_out), .reset(claer));  // open: preset
  D_Flip_Flop d_ff_3 (
    .clk(_3), .D(d_ff_3_qn), .Q(\_3층_LED ), .Qn(d_ff_3_qn), .en(not_1_out), .reset(claer));  // open: preset
  D_Flip_Flop d_ff_4 (
    .clk(_4), .D(d_ff_4_qn), .Q(\_4층_LED ), .Qn(d_ff_4_qn), .en(not_1_out), .reset(claer));  // open: preset
  D_Flip_Flop d_ff_5 (
    .clk(_5), .D(d_ff_5_qn), .Q(\_5층_LED ), .Qn(d_ff_5_qn), .en(not_1_out), .reset(claer));  // open: preset
  D_Flip_Flop d_ff_6 (
    .clk(_6), .D(d_ff_6_qn), .Q(\_6층_LED ), .Qn(d_ff_6_qn), .en(not_1_out), .reset(claer));  // open: preset
  D_Flip_Flop d_ff_7 (
    .clk(_7), .D(d_ff_7_qn), .Q(\_7층_LED ), .Qn(d_ff_7_qn), .en(not_1_out), .reset(claer));  // open: preset
  or or_1 (b0, \_7층_LED , \_5층_LED , \_3층_LED , \_1층_LED );
  or or_2 (b1, \_2층_LED , \_3층_LED , \_6층_LED , \_7층_LED );
  or or_3 (b2, \_4층_LED , \_5층_LED , \_6층_LED , \_7층_LED );
  or or_4 (or_4_out, b0, b2, b1);
  not not_1 (not_1_out, or_4_out);

  // Notes on the sheet:
  //   1
  //   2
  //   4층
  //   3
  //   6
  //   5
  //   7
endmodule

module \_3비트엘리베이터  (
  input  in_1
);

  wire _1_out, _2_out, _3_out, _4_out, _5_out, _6_out, _7_out, and_1_out, and_2_out, clock_1_out,
       clock_2_out, comparator_1_eq, comparator_1_gt, comparator_1_lt, \n7_sd_ff_encoder_1__1층_led ,
       \n7_sd_ff_encoder_1__2층_led , \n7_sd_ff_encoder_1__3층_led , \n7_sd_ff_encoder_1__4층_led ,
       \n7_sd_ff_encoder_1__5층_led , \n7_sd_ff_encoder_1__6층_led , \n7_sd_ff_encoder_1__7층_led ,
       \n7_segment_디코더_1_a_2 , \n7_segment_디코더_1_b_2 , \n7_segment_디코더_1_c_2 , \n7_segment_디코더_1_d ,
       \n7_segment_디코더_1_e , \n7_segment_디코더_1_f , \n7_segment_디코더_1_g ;
  wire [2:0] n3bit_sequential_logic_circuits_1_b0, n7_sd_ff_encoder_1_b0;

  LED led_1 (.in(\n7_sd_ff_encoder_1__5층_led ));
  LED led_2 (.in(\n7_sd_ff_encoder_1__3층_led ));
  LED led_3 (.in(\n7_sd_ff_encoder_1__1층_led ));
  LED led_4 (.in(\n7_sd_ff_encoder_1__7층_led ));
  Button _7 (.out(_7_out));
  Button _5 (.out(_5_out));
  LED led_5 (.in(\n7_sd_ff_encoder_1__6층_led ));
  Button _6 (.out(_6_out));
  LED led_6 (.in(\n7_sd_ff_encoder_1__4층_led ));
  Button _3 (.out(_3_out));
  Button _4 (.out(_4_out));
  Button _1 (.out(_1_out));
  LED led_7 (.in(\n7_sd_ff_encoder_1__2층_led ));
  Button _2 (.out(_2_out));
  and and_1 (and_1_out, comparator_1_eq, clock_1_out);
  Clock clock_1 (.out(clock_1_out));
  _7_sD_FF_ENCODER u_7_sd_ff_encoder_1 (
    ._1(_1_out), ._2(_2_out), ._3(_3_out), ._4(_4_out), ._5(_5_out), ._6(_6_out), ._7(_7_out),
    .claer(and_1_out), .\_1층_LED (\n7_sd_ff_encoder_1__1층_led ), .\_2층_LED (\n7_sd_ff_encoder_1__2층_led ),
    .\_3층_LED (\n7_sd_ff_encoder_1__3층_led ), .\_4층_LED (\n7_sd_ff_encoder_1__4층_led ),
    .\_5층_LED (\n7_sd_ff_encoder_1__5층_led ), .\_6층_LED (\n7_sd_ff_encoder_1__6층_led ),
    .\_7층_LED (\n7_sd_ff_encoder_1__7층_led ), .b2(n7_sd_ff_encoder_1_b0[2]), .b1(n7_sd_ff_encoder_1_b0[1]),
    .b0(n7_sd_ff_encoder_1_b0[0]));
  Clock clock_2 (.out(clock_2_out));
  and and_2 (and_2_out, ~n7_sd_ff_encoder_1_b0[0], ~n7_sd_ff_encoder_1_b0[1], ~n7_sd_ff_encoder_1_b0[2]);  // AND_Gate
  Comparator #(.width(3), .mode("unsigned")) comparator_1 (
    .a(n3bit_sequential_logic_circuits_1_b0), .b(n7_sd_ff_encoder_1_b0), .gt(comparator_1_gt),
    .eq(comparator_1_eq), .lt(comparator_1_lt));
  _3bit_Sequential_Logic_Circuits u_3bit_sequential_logic_circuits_1 (
    .CLOCK(clock_2_out), .Preset(in_1), .B2(n3bit_sequential_logic_circuits_1_b0[2]),
    .B1(n3bit_sequential_logic_circuits_1_b0[1]), .B0(n3bit_sequential_logic_circuits_1_b0[0]),
    .ENABLE(and_2_out), .UP(comparator_1_lt), .DOWN(comparator_1_gt));
  \_7_segment_디코더  \u_7_segment_디코더_1  (
    .A(n3bit_sequential_logic_circuits_1_b0[2]), .B(n3bit_sequential_logic_circuits_1_b0[1]),
    .C(n3bit_sequential_logic_circuits_1_b0[0]), .a_2(\n7_segment_디코더_1_a_2 ), .b_2(\n7_segment_디코더_1_b_2 ),
    .c_2(\n7_segment_디코더_1_c_2 ), .d(\n7_segment_디코더_1_d ), .e(\n7_segment_디코더_1_e ),
    .f(\n7_segment_디코더_1_f ), .g(\n7_segment_디코더_1_g ));
  _7_Segment_Display u_7_segment_display_1 (
    .g(\n7_segment_디코더_1_g ), .f(\n7_segment_디코더_1_f ), .a(\n7_segment_디코더_1_a_2 ),
    .b(\n7_segment_디코더_1_b_2 ), .e(\n7_segment_디코더_1_e ), .d(\n7_segment_디코더_1_d ), .c(\n7_segment_디코더_1_c_2 ));  // open: dp
endmodule
